# Fritzing sketch cassaforte (saved by Fritzing 0.9.0b)
breadboards: 1

parts:
  Componente1 = Arduino Uno (Rev3)
  LED1 = LED - 5mm [color="Red (633nm)" package="5 mm [THT]"]
  R1 = Resistor [tolerance=±5% resistance=220 package=THT]
  J1 = Basic Servo
  Componente2 = Arduino Cap Sense Shield  # not connected

nets:
  N1: Componente1.D9_PWM, J1.pulse
  N2: Componente1.D0/RX, R1.Pin_0
  GND: Componente1.GND, LED1.anode, J1.gnd
  N3: LED1.cathode, R1.Pin_1
